// Logisim project 课设.circ as structural Verilog: 10 circuits, main circuit main
module main (
  input  in_1,
  input  [3:0] in_2,
  input  in_3,
  input  [3:0] in_4,
  input  in_5,
  input  in_6,
  input  in_7,
  output [15:0] out_8,
  output [15:0] out_9,
  output [15:0] \累加器的值 
);

  wire ACen, clock_1_out, clock_2_out, Id, not_1_out, not_2_out, pc_1, Smux, Str, Wpc;
  wire [3:0] \指令译码器_1_s0 ;
  wire [11:0] ADDR;
  wire [15:0] multiplexer_2_out, PC_q, ram_1_data;
  wire [15:12] rom_1_data;

  Clock clock_1 (.out(clock_1_out));
  not not_1 (not_1_out, clock_1_out);
  Counter #(.width(16), .max('hffff)) PC (
    .load(Wpc), .D({in_2, ADDR}), .count(pc_1), .Q(PC_q), .clk(not_1_out), .clr(in_3));  // open: carry
  Hex_Digit_Display hex_digit_display_1 (.value(\累加器的值 [11:8]));  // open: dp
  Hex_Digit_Display hex_digit_display_2 (.value(\累加器的值 [15:12]));  // open: dp
  Hex_Digit_Display hex_digit_display_3 (.value(\累加器的值 [7:4]));  // open: dp
  Hex_Digit_Display hex_digit_display_4 (.value(\累加器的值 [3:0]));  // open: dp
  ROM #(.addrWidth(16), .dataWidth(16)) rom_1 (.addr(PC_q), .data({rom_1_data, ADDR}), .sel(1'b1));
  \指令译码器  \u_指令译码器_1  (
    .OP3(rom_1_data[15]), .OP2(rom_1_data[14]), .OP1(rom_1_data[13]), .OP0(rom_1_data[12]),
    .S3(\指令译码器_1_s0 [3]), .S2(\指令译码器_1_s0 [2]), .S1(\指令译码器_1_s0 [1]), .S0(\指令译码器_1_s0 [0]), .PcAddOne(pc_1),
    .Wpc(Wpc), .Ld(Id), .Str(Str), .Acen(ACen), .Smux(Smux));
  RAM #(.addrWidth(12), .dataWidth(16), .bus("separate")) ram_1 (
    .addr(ADDR), .din(\累加器的值 ), .data(ram_1_data), .str(Str), .sel(1'b1), .ld(Id));  // open: clk, clr
  Register #(.width(16)) AC (.D(multiplexer_2_out), .en(ACen), .Q(\累加器的值 ), .clk(clock_1_out), .clr(in_1));
  Multiplexer #(.select(2)) multiplexer_1 ();  // open: in0, in1, in2, in3, out, sel, en
  \_16位ALU  \u_16位alu_1  (.OP(\指令译码器_1_s0 ), .RS(\累加器的值 ), .RT(ram_1_data), .RD(out_8));  // open: SF, OF, ZF, CF
  Register #(.width(16)) register_1 ();  // open: D, en, Q, clk, clr
  Register #(.width(16)) register_2 ();  // open: D, en, Q, clk, clr
  Register #(.width(16)) register_3 ();  // open: D, en, Q, clk, clr
  Multiplexer #(.width(16)) multiplexer_2 (
    .in0(ram_1_data), .in1(out_8), .out(multiplexer_2_out), .sel(Smux));  // open: en
  not not_2 (not_2_out, in_6);
  Clock clock_2 (.out(clock_2_out));
  RAM #(.addrWidth(4), .dataWidth(16), .bus("separate")) ram_2 (
    .addr(in_4), .din(out_9), .data(out_9), .str(not_2_out), .sel(in_6), .clk(clock_2_out), .ld(in_5));  // open: clr

  // Other names for the same wires on the sheet: AC[15:0] = \累加器的值 

  // Notes on the sheet:
  //   contents of rom_1 (hex, n*v repeats v):
  //   0 4003 5004 6005 7006 2007 8008 1004 1000 0 4000 0 0 4000
endmodule

module \指令译码器  (
  input  OP3,
  input  OP2,
  input  OP1,
  input  OP0,
  output S3,
  output S2,
  output S1,
  output S0,
  output PcAddOne,
  output Wpc,
  output Ld,
  output Str,
  output Acen,
  output Smux
);

  wire and_2_out, and_3_out, and_4_out, and_5_out, and_6_out, not_2_out, not_3_out, not_4_out, not_5_out,
       not_6_out, not_7_out, not_8_out, not_9_out, not_10_out, not_11_out, not_12_out, not_13_out,
       not_14_out, not_15_out, not_16_out, not_17_out, not_18_out, not_19_out;

  not not_1 (S2, OP1);
  and and_1 (S1, OP2, not_2_out);
  not not_2 (not_2_out, OP0);
  not not_3 (not_3_out, OP1);
  or or_1 (S0, not_3_out, not_4_out);
  not not_4 (not_4_out, OP0);
  not not_5 (not_5_out, OP0);
  not not_6 (not_6_out, OP3);
  not not_7 (not_7_out, OP2);
  not not_8 (not_8_out, OP1);
  not not_9 (not_9_out, OP3);
  and and_2 (and_2_out, not_9_out, not_10_out, OP0);
  not not_10 (not_10_out, OP1);
  not not_11 (not_11_out, OP3);
  and and_3 (and_3_out, not_11_out, OP1, not_12_out);
  not not_12 (not_12_out, OP0);
  not not_13 (not_13_out, OP3);
  and and_4 (and_4_out, not_13_out, OP2);
  not not_14 (not_14_out, OP2);
  not not_15 (not_15_out, OP1);
  not not_16 (not_16_out, OP0);
  not not_17 (not_17_out, OP3);
  and and_5 (and_5_out, not_17_out, OP1, not_18_out);
  not not_18 (not_18_out, OP0);
  not not_19 (not_19_out, OP3);
  and and_6 (and_6_out, not_19_out, OP2);
  or or_2 (Smux, OP0, OP1);
  or or_3 (PcAddOne, not_5_out, OP1, OP2, OP3);
  and and_7 (Wpc, not_6_out, not_7_out, not_8_out, OP0);
  or or_4 (Ld, and_2_out, and_3_out, and_4_out);
  and and_8 (Str, OP3, not_14_out, not_15_out, not_16_out);
  or or_5 (Acen, and_5_out, and_6_out);

  assign S3 = 1'b0;
endmodule

// ALU
module \_16位ALU  (
  input  [3:0] OP,
  input  [15:0] RS,
  input  [15:0] RT,
  output SF,
  output OF,
  output ZF,
  output CF,
  output [15:0] RD
);

  wire n74ls181_1_cn_4, n74ls181_2_cn_4, n74ls181_3_cn_4, n74ls181_4_cn_4, \n74ls181功能选择信号形成电路_1_cn ,
       \n74ls181功能选择信号形成电路_1_m , not_1_out;
  wire [1:0] \n74ls181功能选择信号形成电路_1_sel0 ;
  wire [2:0] n74ls181_1_f;
  wire [3:0] n74ls181_2_f, n74ls181_3_f, n74ls181_4_f, \n74ls181功能选择信号形成电路_1_s00 ;
  wire [15:0] shifter_1_out, shifter_2_out, shifter_3_out;

  \_74LS181功能选择信号形成电路  \u_74ls181功能选择信号形成电路_1  (
    .S3(OP[3]), .S2(OP[2]), .S1(OP[1]), .S0(OP[0]), .Cn(\n74ls181功能选择信号形成电路_1_cn ),
    .M(\n74ls181功能选择信号形成电路_1_m ), .S30(\n74ls181功能选择信号形成电路_1_s00 [3]), .S20(\n74ls181功能选择信号形成电路_1_s00 [2]),
    .S10(\n74ls181功能选择信号形成电路_1_s00 [1]), .S00(\n74ls181功能选择信号形成电路_1_s00 [0]),
    .SEL1(\n74ls181功能选择信号形成电路_1_sel0 [1]), .SEL0(\n74ls181功能选择信号形成电路_1_sel0 [0]));
  _74LS181 u_74ls181_1 (
    .A(RS[15:12]), .B(RT[15:12]), .Cn(n74ls181_2_cn_4), .M(\n74ls181功能选择信号形成电路_1_m ), .Cn_4(n74ls181_1_cn_4),
    .S3_S0(\n74ls181功能选择信号形成电路_1_s00 ), .F({SF, n74ls181_1_f}));  // open: A_B, P, G
  _74LS181 u_74ls181_2 (
    .A(RS[11:8]), .B(RT[11:8]), .Cn(n74ls181_3_cn_4), .M(\n74ls181功能选择信号形成电路_1_m ), .Cn_4(n74ls181_2_cn_4),
    .S3_S0(\n74ls181功能选择信号形成电路_1_s00 ), .F(n74ls181_2_f));  // open: A_B, P, G
  Shifter #(.width(16)) shifter_1 (.in(RS), .\dist (RT[3:0]), .out(shifter_1_out));
  Shifter #(.width(16), .shift("lr")) shifter_2 (.in(RS), .\dist (RT[3:0]), .out(shifter_2_out));
  Shifter #(.width(16), .shift("ar")) shifter_3 (.in(RS), .\dist (RT[3:0]), .out(shifter_3_out));
  _74LS181 u_74ls181_3 (
    .A(RS[7:4]), .B(RT[7:4]), .Cn(n74ls181_4_cn_4), .M(\n74ls181功能选择信号形成电路_1_m ), .Cn_4(n74ls181_3_cn_4),
    .S3_S0(\n74ls181功能选择信号形成电路_1_s00 ), .F(n74ls181_3_f));  // open: A_B, P, G
  Multiplexer #(.select(2), .width(16)) multiplexer_1 (
    .in0({SF, n74ls181_1_f, n74ls181_2_f, n74ls181_3_f, n74ls181_4_f}), .in1(shifter_1_out),
    .in2(shifter_2_out), .in3(shifter_3_out), .out({{2{RD[15]}}, RD[13:0]}),
    .sel(\n74ls181功能选择信号形成电路_1_sel0 ), .en(1'b1));
  _74LS181 u_74ls181_4 (
    .A(RS[3:0]), .B(RT[3:0]), .Cn(\n74ls181功能选择信号形成电路_1_cn ), .M(\n74ls181功能选择信号形成电路_1_m ),
    .Cn_4(n74ls181_4_cn_4), .S3_S0(\n74ls181功能选择信号形成电路_1_s00 ), .F(n74ls181_4_f));  // open: A_B, P, G
  \OF标志形成电路  \of标志形成电路_1  (.SUB(OP[0]), .Fa(RS[15]), .Fb(RT[15]), .Ff(SF), .OF(OF));
  not not_1 (not_1_out, n74ls181_1_cn_4);
  \ZF标志形成电路  \zf标志形成电路_1  (
    .f15(RD[15]), .f14(RD[15]), .f13(RD[13]), .f12(RD[12]), .f11(RD[11]), .f10(RD[10]), .f9(RD[9]),
    .f8(RD[8]), .f7(RD[7]), .f6(RD[6]), .f5(RD[5]), .f4(RD[4]), .f3(RD[3]), .f2(RD[2]), .f1(RD[1]),
    .f0(RD[0]), .ZF(ZF));
  xor xor_1 (CF, OP[0], not_1_out);

  assign RD[14] = RD[15];
endmodule

module \OF标志形成电路  (
  input  SUB,
  input  Fa,
  input  Fb,
  input  Ff,
  output OF
);

  wire and_1_out, and_2_out, and_3_out, and_4_out, not_1_out, not_2_out, not_3_out, not_4_out, not_5_out,
       not_6_out, not_7_out, not_8_out;

  not not_1 (not_1_out, SUB);
  not not_2 (not_2_out, Fa);
  not not_3 (not_3_out, Fb);
  not not_4 (not_4_out, SUB);
  not not_5 (not_5_out, Ff);
  not not_6 (not_6_out, Fa);
  not not_7 (not_7_out, Fb);
  not not_8 (not_8_out, Ff);
  and and_1 (and_1_out, not_1_out, not_2_out, not_3_out, Ff);
  and and_2 (and_2_out, not_4_out, Fa, Fb, not_5_out);
  and and_3 (and_3_out, SUB, not_6_out, Fb, Ff);
  and and_4 (and_4_out, SUB, Fa, not_7_out, not_8_out);
  or or_1 (OF, and_1_out, and_2_out, and_3_out, and_4_out);
endmodule

module \ZF标志形成电路  (
  input  f15,
  input  f14,
  input  f13,
  input  f12,
  input  f11,
  input  f10,
  input  f9,
  input  f8,
  input  f7,
  input  f6,
  input  f5,
  input  f4,
  input  f3,
  input  f2,
  input  f1,
  input  f0,
  output ZF
);

  wire and_1_out, and_2_out, and_3_out, and_4_out, not_1_out, not_2_out, not_3_out, not_4_out, not_5_out,
       not_6_out, not_7_out, not_8_out, not_9_out, not_10_out, not_11_out, not_12_out, not_13_out,
       not_14_out, not_15_out, not_16_out;

  not not_1 (not_1_out, f15);
  not not_2 (not_2_out, f14);
  not not_3 (not_3_out, f13);
  not not_4 (not_4_out, f12);
  not not_5 (not_5_out, f11);
  not not_6 (not_6_out, f10);
  not not_7 (not_7_out, f9);
  not not_8 (not_8_out, f8);
  not not_9 (not_9_out, f7);
  not not_10 (not_10_out, f6);
  not not_11 (not_11_out, f5);
  not not_12 (not_12_out, f4);
  not not_13 (not_13_out, f3);
  not not_14 (not_14_out, f2);
  not not_15 (not_15_out, f1);
  not not_16 (not_16_out, f0);
  and and_1 (and_1_out, not_1_out, not_2_out, not_3_out, not_4_out);
  and and_2 (and_2_out, not_5_out, not_6_out, not_7_out, not_8_out);
  and and_3 (and_3_out, not_9_out, not_10_out, not_11_out, not_12_out);
  and and_4 (and_4_out, not_13_out, not_14_out, not_15_out, not_16_out);
  and and_5 (ZF, and_1_out, and_2_out, and_3_out, and_4_out);
endmodule

module \_74LS181功能选择信号形成电路  (
  input  S3,
  input  S2,
  input  S1,
  input  S0,
  output Cn,
  output M,
  output S30,
  output S20,
  output S10,
  output S00,
  output SEL1,
  output SEL0
);

  wire and_1_out, and_2_out, and_5_out, and_6_out, and_7_out, and_8_out, and_9_out, not_1_out, not_2_out,
       not_3_out, not_4_out, not_5_out, not_6_out, not_7_out, not_8_out, not_9_out, not_10_out;

  not not_1 (not_1_out, S1);
  and and_1 (and_1_out, not_1_out, not_2_out);
  not not_2 (not_2_out, S0);
  and and_2 (and_2_out, S1, S0);
  not not_3 (not_3_out, S2);
  and and_3 (S30, not_3_out, not_4_out);
  not not_4 (not_4_out, S0);
  not not_5 (not_5_out, S1);
  and and_4 (S20, not_5_out, S0);
  not not_6 (not_6_out, S1);
  and and_5 (and_5_out, not_6_out, S0);
  and and_6 (and_6_out, S1, not_7_out);
  not not_7 (not_7_out, S0);
  not not_8 (not_8_out, S2);
  and and_7 (and_7_out, not_8_out, not_9_out);
  not not_9 (not_9_out, S0);
  and and_8 (and_8_out, S2, S1, S0);
  and and_9 (and_9_out, S2, S1, not_10_out);
  not not_10 (not_10_out, S0);
  or or_1 (Cn, and_1_out, and_2_out);
  or or_2 (S10, and_5_out, and_6_out);
  or or_3 (S00, and_7_out, S1);
  or or_4 (SEL1, and_8_out, S3);
  or or_5 (SEL0, and_9_out, S3);

  assign M = S2;
endmodule

module _74LS181 (
  input  [3:0] A,
  input  [3:0] B,
  input  Cn,
  input  M,
  input  [3:0] S3_S0,
  output A_B,
  output P,
  output Cn_4,
  output G,
  output [3:0] F
);

  wire and_1_out, and_2_out, and_3_out, and_4_out, and_5_out, and_6_out, and_7_out, and_8_out, and_9_out,
       and_10_out, and_12_out, and_13_out, and_14_out, and_15_out, and_16_out, and_17_out, and_18_out,
       and_19_out, and_20_out, and_21_out, and_22_out, and_23_out, and_24_out, and_25_out, and_26_out,
       and_27_out, and_28_out, and_29_out, and_30_out, and_31_out, and_32_out, and_33_out, and_34_out,
       and_35_out, and_36_out, and_37_out, and_38_out, nand_1_out, nand_3_out, nor_1_out, nor_2_out,
       nor_3_out, nor_4_out, nor_5_out, nor_6_out, nor_7_out, nor_8_out, nor_9_out, nor_10_out, nor_11_out,
       nor_12_out, not_1_out, not_2_out, not_3_out, not_4_out, not_5_out, not_6_out, not_7_out, not_8_out,
       not_9_out;

  not not_1 (not_1_out, M);
  and and_1 (and_1_out, A[0], A[0]);
  nand nand_1 (nand_1_out, Cn, not_1_out);
  xor xor_1 (F[0], nand_1_out, and_5_out);
  and and_2 (and_2_out, S3_S0[1], not_3_out);
  and and_3 (and_3_out, B[0], S3_S0[0]);
  nor nor_1 (nor_1_out, and_1_out, and_3_out, and_2_out);
  and and_4 (and_4_out, not_1_out, nor_1_out);
  not not_2 (not_2_out, nor_1_out);
  and and_5 (and_5_out, not_2_out, nor_2_out);
  not not_3 (not_3_out, B[0]);
  and and_6 (and_6_out, not_3_out, S3_S0[2], A[0]);
  nor nor_2 (nor_2_out, and_6_out, and_8_out);
  and and_7 (and_7_out, not_1_out, nor_2_out, Cn);
  nor nor_3 (nor_3_out, and_4_out, and_7_out);
  xor xor_2 (F[1], nor_3_out, and_10_out);
  and and_8 (and_8_out, A[0], B[0], S3_S0[3]);
  and and_9 (and_9_out, A[1], A[1]);
  not not_4 (not_4_out, nor_4_out);
  and and_10 (and_10_out, not_4_out, nor_6_out);
  // Probe on nor_5_out
  and and_11 (A_B, F[0], F[1], F[2], F[3]);
  and and_12 (and_12_out, B[1], S3_S0[0]);
  and and_13 (and_13_out, S3_S0[1], not_5_out);
  nor nor_4 (nor_4_out, and_9_out, and_12_out, and_13_out);
  and and_14 (and_14_out, not_1_out, nor_1_out, nor_6_out);
  and and_15 (and_15_out, not_1_out, nor_4_out);
  nor nor_5 (nor_5_out, and_15_out, and_14_out, and_17_out);
  xor xor_3 (F[2], nor_5_out, and_18_out);
  not not_5 (not_5_out, B[1]);
  and and_16 (and_16_out, not_5_out, S3_S0[2], A[1]);
  nor nor_6 (nor_6_out, and_16_out, and_19_out);
  and and_17 (and_17_out, not_1_out, Cn, nor_2_out, nor_6_out);
  not not_6 (not_6_out, nor_7_out);
  and and_18 (and_18_out, not_6_out, nor_9_out);
  // Probe on F[2]
  // Probe on B[3]
  and and_19 (and_19_out, A[1], B[1], S3_S0[3]);
  and and_20 (and_20_out, A[2], A[2]);
  and and_21 (and_21_out, not_1_out, nor_7_out);
  and and_22 (and_22_out, not_1_out, nor_4_out, nor_9_out);
  and and_23 (and_23_out, S3_S0[1], not_7_out);
  and and_24 (and_24_out, B[2], S3_S0[0]);
  nor nor_7 (nor_7_out, and_20_out, and_24_out, and_23_out);
  and and_25 (and_25_out, not_1_out, nor_1_out, nor_6_out, nor_9_out);
  nor nor_8 (nor_8_out, and_21_out, and_22_out, and_25_out, and_27_out);
  xor xor_4 (F[3], nor_8_out, and_28_out);
  not not_7 (not_7_out, B[2]);
  and and_26 (and_26_out, not_7_out, S3_S0[2], A[2]);
  nor nor_9 (nor_9_out, and_26_out, and_30_out);
  and and_27 (and_27_out, not_1_out, Cn, nor_2_out, nor_6_out, nor_9_out);
  not not_8 (not_8_out, nor_10_out);
  and and_28 (and_28_out, not_8_out, nor_11_out);
  and and_29 (and_29_out, A[3], A[3]);
  and and_30 (and_30_out, A[2], B[2], S3_S0[3]);
  nand nand_2 (P, nor_2_out, nor_6_out, nor_9_out, nor_11_out);
  and and_31 (and_31_out, B[3], S3_S0[0]);
  and and_32 (and_32_out, S3_S0[1], not_9_out);
  nor nor_10 (nor_10_out, and_29_out, and_31_out, and_32_out);
  nand nand_3 (nand_3_out, Cn, nor_2_out, nor_6_out, nor_9_out, nor_11_out);
  or or_1 (Cn_4, ~nand_3_out, ~nor_12_out);  // OR_Gate
  not not_9 (not_9_out, B[3]);
  and and_33 (and_33_out, not_9_out, S3_S0[2], A[3]);
  nor nor_11 (nor_11_out, and_33_out, and_36_out);
  and and_34 (and_34_out, nor_4_out, nor_9_out, nor_11_out);
  and and_35 (and_35_out, nor_1_out, nor_6_out, nor_9_out, nor_11_out);
  nor nor_12 (nor_12_out, and_35_out, and_34_out, and_37_out, and_38_out);
  not not_10 (G, nor_12_out);
  and and_36 (and_36_out, A[3], B[3], S3_S0[3]);
  and and_37 (and_37_out, nor_7_out, nor_11_out);
  and and_38 (and_38_out, nor_10_out, nor_10_out);
  // Probe on B[3]
endmodule

module test (
  input  [3:0] in_1,
  input  [5:0] in_2,
  input  [15:0] in_3,
  input  in_4,
  input  in_5,
  input  in_6,
  output [15:0] out_7,
  output [15:0] out_8,
  output [15:0] out_9
);

  wire clock_1_out, not_1_out;
  wire [2:0] \test2_1_载入值 ;
  wire [15:0] _01_q, _02_q, _03_q, multiplexer_1_out, \n16位alu_1_rd , ram_1_data;

  Clock clock_1 (.out(clock_1_out));
  not not_1 (not_1_out, in_4);
  \_16位ALU  \u_16位alu_1  (.OP(in_1), .RS(out_7), .RT(out_8), .RD(\n16位alu_1_rd ));  // open: SF, OF, ZF, CF
  RAM #(.addrWidth(16), .dataWidth(16), .bus("separate")) ram_1 (
    .addr(in_3), .data(ram_1_data), .str(not_1_out), .sel(1'b1), .clk(clock_1_out), .ld(in_4));  // open: din, clr
  Multiplexer #(.width(16)) multiplexer_1 (
    .in0(ram_1_data), .in1(\n16位alu_1_rd ), .out(multiplexer_1_out), .sel(in_5));  // open: en
  Register #(.width(16)) _01 (.D(multiplexer_1_out), .en(\test2_1_载入值 [0]), .Q(_01_q), .clk(clock_1_out), .clr(in_6));
  test2 test2_1 (
    .\_01寄存器值 (_01_q), .\_02寄存器值 (_02_q), .\_03寄存器值 (_03_q), .in_4(in_2), .S(out_7), .R(out_8), .D(out_9),
    .\载入值 (\test2_1_载入值 ));
  Register #(.width(16)) _02 (.D(multiplexer_1_out), .en(\test2_1_载入值 [1]), .Q(_02_q), .clk(clock_1_out), .clr(in_6));
  Register #(.width(16)) _03 (.D(multiplexer_1_out), .en(\test2_1_载入值 [2]), .Q(_03_q), .clk(clock_1_out), .clr(in_6));

  // Other names for the same wires on the sheet: RD[15:0] = out_9; RS[15:0] = out_7; RT[15:0] = out_8
endmodule

module test2 (
  input  [15:0] \_01寄存器值 ,
  input  [15:0] \_02寄存器值 ,
  input  [15:0] \_03寄存器值 ,
  input  [5:0] in_4,
  output [15:0] S,
  output [15:0] R,
  output [15:0] D,
  output [2:0] \载入值 
);

  Multiplexer #(.select(2), .width(16)) multiplexer_1 (
    .in1(\_01寄存器值 ), .in2(\_02寄存器值 ), .in3(\_03寄存器值 ), .out(S), .sel(in_4[5:4]));  // open: in0, en
  Multiplexer #(.select(2), .width(16)) multiplexer_2 (
    .in1(\_01寄存器值 ), .in2(\_02寄存器值 ), .in3(\_03寄存器值 ), .out(R), .sel(in_4[3:2]));  // open: in0, en
  Multiplexer #(.select(2), .width(16)) multiplexer_3 (
    .in1(\_01寄存器值 ), .in2(\_02寄存器值 ), .in3(\_03寄存器值 ), .out(D), .sel(in_4[1:0]));  // open: in0, en
  test3 test3_1 (
    .RS1(in_4[5]), .RS0(in_4[4]), .RT1(in_4[3]), .RT0(in_4[2]), .RD1(in_4[1]), .RD0(in_4[0]), .R1(\载入值 [0]),
    .R2(\载入值 [1]), .R3(\载入值 [2]));
endmodule

module test3 (
  input  RS1,
  input  RS0,
  input  RT1,
  input  RT0,
  input  RD1,
  input  RD0,
  output R1,
  output R2,
  output R3
);

  wire and_1_out, and_2_out, and_3_out, and_4_out, and_5_out, and_6_out, and_7_out, and_8_out, and_9_out,
       not_1_out, not_2_out, not_3_out, not_4_out, not_5_out, not_6_out;

  not not_1 (not_1_out, RS1);
  not not_2 (not_2_out, RT1);
  not not_3 (not_3_out, RD1);
  not not_4 (not_4_out, RS0);
  not not_5 (not_5_out, RT0);
  not not_6 (not_6_out, RD0);
  and and_1 (and_1_out, RS1, RS0);
  and and_2 (and_2_out, RT1, RT0);
  and and_3 (and_3_out, RD1, RD0);
  and and_4 (and_4_out, not_1_out, RS0);
  and and_5 (and_5_out, not_2_out, RT0);
  and and_6 (and_6_out, not_3_out, RD0);
  and and_7 (and_7_out, RS1, not_4_out);
  and and_8 (and_8_out, RT1, not_5_out);
  and and_9 (and_9_out, RD1, not_6_out);
  or or_1 (R3, and_1_out, and_2_out, and_3_out);
  or or_2 (R1, and_4_out, and_5_out, and_6_out);
  or or_3 (R2, and_7_out, and_8_out, and_9_out);
endmodule
